// Digital circuit CompleteComputer.dig as structural Verilog
module CompleteComputer (
  input  CLK,
  input  RST
);

  wire ALU_p5, c, not_1_out, steuerwerk_1_p1, steuerwerk_1_p4, steuerwerk_1_p5, steuerwerk_1_p6,
       steuerwerk_1_p7, steuerwerk_1_p8, steuerwerk_1_p9, steuerwerk_1_p10, steuerwerk_1_p11,
       steuerwerk_1_p12, steuerwerk_1_p13;
  wire [6:0] multiplexer_1_out;
  wire [7:0] ALU_p3, AR_p3, IR_p5, PC_a_out;
  wire [7:7] multiplexer_1_out_2;

  and and_1 (c, CLK, ~RST);  // And
  // Steuerwerk steuerwerk_1: pin names not known; wires that end beside it: steuerwerk_1_p1, c, RST, steuerwerk_1_p4, steuerwerk_1_p5, steuerwerk_1_p6, steuerwerk_1_p7, steuerwerk_1_p8, steuerwerk_1_p9, steuerwerk_1_p10, steuerwerk_1_p11, steuerwerk_1_p12, steuerwerk_1_p13
  LED led_1 (.in(steuerwerk_1_p4));
  LED led_2 (.in(steuerwerk_1_p5));
  LED led_3 (.in(steuerwerk_1_p6));
  // Probe on steuerwerk_1_p1
  // _8_Bit_Register IR: pin names not known; wires that end beside it: RST, c, steuerwerk_1_p1, steuerwerk_1_p4, IR_p5
  // _8_Bit_Register AR: pin names not known; wires that end beside it: RST, c, AR_p3, steuerwerk_1_p5, IR_p5
  // Probe on AR_p3
  \_8_Bit_Zählregister  PC (
    .A_IN(AR_p3), .INC(steuerwerk_1_p10), .EN(steuerwerk_1_p11), .CLK(c), .RST(RST), .A_out(PC_a_out));
  // Probe on PC_a_out
  // Probe on steuerwerk_1_p7
  Multiplexer #(.Bits(8)) multiplexer_1 (
    .sel(steuerwerk_1_p12), .in_0(AR_p3), .in_1(PC_a_out), .out({multiplexer_1_out_2[7], multiplexer_1_out}));
  // ALU_8Bit_Complete_Computer ALU: pin names not known; wires that end beside it: steuerwerk_1_p7, IR_p5, ALU_p3, steuerwerk_1_p8, ALU_p5
  // _8_Bit_Register Akku: pin names not known; wires that end beside it: ALU_p5, steuerwerk_1_p9, c, RST, ALU_p3
  not not_1 (not_1_out, multiplexer_1_out_2[7]);
  // Probe on ALU_p3
  ROM #(.AddrBits(7), .Bits(8)) rom_1 (.A(multiplexer_1_out), .sel(not_1_out), .D(IR_p5));
  RAMDualPort #(.AddrBits(7), .Bits(8)) ramdualport_1 (
    .A(multiplexer_1_out), .Din(ALU_p3), .str(steuerwerk_1_p13), .C(c), .ld(multiplexer_1_out_2[7]), .D(IR_p5));
  // Probe on IR_p5

  // Other names for the same wires on the sheet: r = RST

  // Notes on the sheet:
  //   contents of rom_1 (hex, n*v repeats v):
  //   1,0,1,0,1,0,1
endmodule
